# Fritzing sketch RFCar (saved by Fritzing 0.9.3b)
breadboards: 1

parts:
  IC1 = H-Bridge [package=THT]
  M1 = DC Motor
  M2 = DC Motor
  Part1 = Arduino Uno (Rev3)
  VCC1 = Battery block 9V

nets:
  N1: IC1.1_2EN, IC1.3_4EN, IC1.VCC1, Part1.5V
  N2: IC1.1A, Part1.D11_PWM/MOSI
  N3: IC1.1Y, M2.pin_2
  GND1: IC1.GND1, IC1.GND2, IC1.GND3, IC1.GND4, Part1.GND, VCC1.-
  N4: IC1.2Y, M2.pin_1
  N5: IC1.2A, Part1.D10_PWM/SS
  N6: IC1.VCC2, VCC1.+
  N7: IC1.3A, Part1.D3_PWM
  N8: IC1.3Y, M1.pin_2
  N9: IC1.4Y, M1.pin_1
  N10: IC1.4A, Part1.D2
